# Fritzing sketch device_bebe_breadboard (saved by Fritzing 0.8.5b)
breadboards: 1

parts:
  Atmega1 = ATmega644 [package=pdpi]
  U1 = microSD Socket [package=usd-socket-pp]  # not connected
  U2 = 3.5mm Audio Jack [package=audio-jack-3.5mm-smd]  # not connected
  Y1 = CRYSTAL [package=hc49up]
  C1 = Capacitor [package=cap-pth-small2]
  C2 = Capacitor [package=cap-pth-small2]
  C3 = Capacitor [package=cap-pth-small2]
  C4 = Capacitor [package=cap-pth-small2]
  C5 = Capacitor [package=cap-pth-small]  # not connected
  C6 = Capacitor [package=cap-pth-small]  # not connected
  R1 = Resistor [tolerance=±5% resistance=10k package=THT]
  U3 = DS1307 [package=so08]  # not connected

nets:
  N1: Atmega1.PD1, R1.Pin_0
  N2: Atmega1.PD5, R1.Pin_1
  N3: Atmega1.PC1, C4.2
  N4: Atmega1.PC3, C4.1
  N5: Atmega1.PC4, C3.2
  N6: Atmega1.PC6, C3.1
  N7: Atmega1.PC7, C2.2
  N8: Atmega1.GND#30, C2.1
  N9: Atmega1.AREF, C1.2
  N10: Atmega1.PA6, C1.1
  N11: Atmega1.PA3, Y1.2
  N12: Atmega1.PA1, Y1.1
